# Fritzing sketch Untitled Sketch (saved by Fritzing 0.9.0b)
breadboards: 1

parts:
  part = Arduino Pro Mini v13
  part_2 = LCD-16X2 [package=lcd-8x2-kit]
  part_3 = 74HC595 [package="DIP16 [THT]"]
  part_4 = smd LED [color="Red (633nm)" package="0805 [SMD]"]
  part_5 = 74HC595 [package="DIP16 [THT]"]
  R1 = Resistor [tolerance=±5% resistance=220 package=THT]
  part_6 = 74HC595 [package="DIP16 [THT]"]
  LED1 = LED - 5mm [color="Red (633nm)" package="5 mm [THT]"]
  LED2 = LED - 5mm [color="Red (633nm)" package="5 mm [THT]"]
  LED3 = LED - 5mm [color="Red (633nm)" package="5 mm [THT]"]
  LED4 = LED - 5mm [color="Red (633nm)" package="5 mm [THT]"]
  LED5 = LED - 5mm [color="Red (633nm)" package="5 mm [THT]"]
  LED6 = LED - 5mm [color="Red (633nm)" package="5 mm [THT]"]
  LED7 = LED - 5mm [color="Red (633nm)" package="5 mm [THT]"]
  LED8 = LED - 5mm [color="Red (633nm)" package="5 mm [THT]"]
  R2 = Resistor [tolerance=±5% resistance=220 package=THT]
  R3 = Resistor [tolerance=±5% resistance=220 package=THT]
  R6 = Resistor [tolerance=±5% resistance=220 package=THT]
  R7 = Resistor [tolerance=±5% resistance=220 package=THT]
  R8 = Resistor [tolerance=±5% resistance=220 package=THT]
  R9 = Resistor [tolerance=±5% resistance=220 package=THT]
  R10 = Resistor [tolerance=±5% resistance=220 package=THT]
  R11 = Resistor [tolerance=±5% resistance=220 package=THT]
  LED9 = LED - 5mm [color="Red (633nm)" package="5 mm [THT]"]
  LED10 = LED - 5mm [color="Red (633nm)" package="5 mm [THT]"]
  LED11 = LED - 5mm [color="Red (633nm)" package="5 mm [THT]"]
  LED12 = LED - 5mm [color="Red (633nm)" package="5 mm [THT]"]
  LED13 = LED - 5mm [color="Red (633nm)" package="5 mm [THT]"]
  LED14 = LED - 5mm [color="Red (633nm)" package="5 mm [THT]"]
  LED15 = LED - 5mm [color="Red (633nm)" package="5 mm [THT]"]
  LED16 = LED - 5mm [color="Red (633nm)" package="5 mm [THT]"]
  R12 = Resistor [tolerance=±5% resistance=220 package=THT]
  R13 = Resistor [tolerance=±5% resistance=220 package=THT]
  R14 = Resistor [tolerance=±5% resistance=220 package=THT]
  R15 = Resistor [tolerance=±5% resistance=220 package=THT]
  R16 = Resistor [tolerance=±5% resistance=220 package=THT]
  R17 = Resistor [tolerance=±5% resistance=220 package=THT]
  R18 = Resistor [tolerance=±5% resistance=220 package=THT]
  R19 = Resistor [tolerance=±5% resistance=220 package=THT]

nets:
  5V: part.VCC, part_2.VDD, part_3.MR, part_3.VCC, part_4.anode, part_5.MR, part_5.VCC, part_6.MR, part_6.VCC
  GND: part.GND, part_2.VSS, part_2.R_W, part_2.K, part_3.GND, part_3.OE, part_5.GND, part_5.OE, R1.Pin_1, part_6.GND, part_6.OE, R2.Pin_1, R3.Pin_1, R6.Pin_1, R7.Pin_1, R8.Pin_1, R9.Pin_1, R10.Pin_1, R11.Pin_1, R12.Pin_1, R13.Pin_1, R14.Pin_1, R15.Pin_1, R16.Pin_1, R17.Pin_1, R18.Pin_1, R19.Pin_1
  N1: part.D9_PWM, part_5.ST_CP
  N2: part.D8, part_3.SH_CP, part_5.SH_CP, part_6.SH_CP
  N3: part.D7, part_3.DS, part_5.DS, part_6.DS
  N4: part.D2, part_2.E, part_3.ST_CP
  N5: part_2.VO, R1.Pin_0
  N6: part_2.RS, part_3.Q2
  N7: part_2.DB4, part_3.Q3
  N8: part_2.DB5, part_3.Q4
  N9: part_2.DB6, part_3.Q5
  N10: part_2.DB7, part_3.Q6
  N11: part_2.A, part_4.cathode
  N12: part_5.Q1, LED8.anode
  N13: part_5.Q2, LED6.anode
  N14: part_5.Q3, LED7.anode
  N15: part_5.Q4, LED4.anode
  N16: part_5.Q5, LED3.anode
  N17: part_5.Q6, LED2.anode
  N18: part_5.Q7, LED1.anode
  N19: part_5.Q7', part_6.ST_CP
  N20: part_5.Q0, LED5.anode
  N21: part_6.Q1, LED9.anode
  N22: part_6.Q2, LED12.anode
  N23: part_6.Q3, LED16.anode
  N24: part_6.Q4, LED10.anode
  N25: part_6.Q5, LED15.anode
  N26: part_6.Q6, LED13.anode
  N27: part_6.Q7, LED11.anode
  N28: part_6.Q0, LED14.anode
